# Fritzing sketch Schaltplan (saved by Fritzing 1.0.6)
stripboards: 2

parts:
  A1 = XIAO ESP32C3-tht
  Arduino_CNC_Shield_V3_00_1 = Arduino_CNC_V3.00
  Bauteil1 = Arduino Uno (Rev3)
  U1 = LM2596 step down module
  U2 = LM2596 step down module
  BAT1 = Lithium Ion Polymer Battery 11.1v 5000mah
  U3 = ESP32-38PinWide [part_number=ESP32-38PinWide]
  Bauteil2 = Arduino Uno (Rev3)
  Bauteil3 = Arduino Uno (Rev3)
  A2 = ELRS EP2 Receiver
  Arduino_CNC_Shield_V3_00_2 = Arduino_CNC_V3.00
  Arduino_CNC_Shield_V3_00_3 = Arduino_CNC_V3.00
  Mod1 = KY-019 5V Relay Module [package="Breakout board"]
  C1 = Electrolytic Capacitor [capacitance=0.5mF voltage=35V package="100 mil [THT, electrolytic]"]
  C2 = Electrolytic Capacitor [capacitance=0.5mF voltage=35V package="100 mil [THT, electrolytic]"]
  C3 = Electrolytic Capacitor [capacitance=100nF voltage=35V package="100 mil [THT, electrolytic]"]

nets:
  N1: A1.Pin_12, A2.RX
  N2: A1.Pin_13, A2.TX
  N3: A1.Pin_15, Bauteil1.D0/RX, U3.GPIO14, Bauteil2.D0/RX, Bauteil3.D0/RX
  GND: A1.Pin_21, Arduino_CNC_Shield_V3_00_1.POWER_-, Bauteil1.GND, U1.IN-, U1.OUT-, U2.IN-, U2.OUT-, BAT1.negative, U3.GND, Bauteil2.GND, Bauteil3.GND, A2.GND, Arduino_CNC_Shield_V3_00_2.POWER_-, Arduino_CNC_Shield_V3_00_3.POWER_-, Mod1.-, C1.-, C2.-, C3.+
  5V: A1.Pin_22, Bauteil1.5V, U1.OUT+, U3.VIN, Bauteil2.5V, Bauteil3.5V, A2.5V, Mod1.+, C1.+, C2.+
  N4: Arduino_CNC_Shield_V3_00_1.POWER_+, Arduino_CNC_Shield_V3_00_2.POWER_+, Arduino_CNC_Shield_V3_00_3.POWER_+, Mod1.NO
  N5: U1.IN+, U2.IN+, BAT1.positive, Mod1.Common
  N6: U2.OUT+, C3.-
  N7: Bauteil3.D3_PWM, Mod1.S

notes:
  12V Step Down 5V

custom parts:
  XIAO ESP32C3-tht: Seeed Studio XIAO ESP32C3 adopts new RISC-V architecture, supporting both Wi-Fi and BLE wireless connectivities.
  Arduino_CNC_V3.00: Protoneer Arduino CNC Shield V3.00 If using Grbl V0.9: The “A” axis can not be used (yet). The “SCL” (Arduino A5) pin is now used for 'Probing' input. The “End Stops Z+ & Z-” (Arduino D11) and “SpnEn” (Arduino D12) have been switched!
  LM2596 step down module: LM2596 DC-DC step down power supply module 3 A.
  ESP32-38PinWide: Generic 38-Pin ESP32 with wide format (only access to one side of pins on a breadboard) based on Stephen Lilley's HiLetgo ESP-WROOM-32 ESP32 ESP-32S Development Board.
  ELRS EP2 Receiver: ELRS EP2 Receiver by HappyModel
  KY-019 5V Relay Module: KY-019 5V Relay module, used to control AC circuits. (Special thanks to vanepp for fixing the PCB holes and other errors)
